# Fritzing sketch Early PCB design (saved by Fritzing 0.9.5d)
circuit board: 12.9065cm x 8.74508cm
breadboards: 1

parts:
  Power_plug1 = Power plug
  IR_Sensor = Infrared Proximity Sensor
  Servo_Motor = Basic Servo
  Part1 = Arduino Uno (Rev3)

nets:
  GND: Power_plug1.GND, IR_Sensor.GND, Servo_Motor.gnd, Part1.GND
  VCC: Power_plug1.VCC, IR_Sensor.Vcc, Servo_Motor.vcc, Servo_Motor.pulse, Part1.D9_PWM, Part1.5V
  N1: IR_Sensor.Vout, Part1.D2
